// Logisim project ac01.circ as structural Verilog
module memRAMq2 (
  input  [4:0] in_1,
  input  in_2,
  input  in_3,
  input  [23:0] in_4,
  input  in_5,
  output [23:0] out_6
);

  RAM #(.addrWidth(5), .dataWidth(24)) ram_1 (.addr(in_1), .we(in_2), .oe(in_3), .clk(in_5), .din(in_4), .dout(out_6));

  // Notes on the sheet:
  //   a) 5
  //   b) Os valores foram reiniciados para 0
  //   c) Sim
  //   d) Cada endereço agora possui mais 12 bits de informaçao
  //   e) A propriedade determina se eh possivel a leitura/ escrita na RAM sem que haja sinal de clock
endmodule

module memROMq1 (
  input  [4:0] in_1,
  output [11:0] out_2
);

  ROM #(.addrWidth(5), .dataWidth(12)) rom_1 (.addr(in_1), .data(out_2));

  // Notes on the sheet:
  //   c) Permanecem
  //   a) 12 * 32 = 384 bits
  //   contents of rom_1 (hex, n*v repeats v):
  //   363 3d6 74 5 5 f 898 55 e4 e 0 46 a 54f a3 3 f3 33 536 57d e 98e 54 0 3 8 689 68 a 898 745 a
endmodule

module memRAMq3 (
  input  [6:0] in_1,
  input  [7:0] in_2,
  input  in_3,
  input  [6:0] in_4,
  output [3:0] MaisSignificativa,
  output [7:0] out_6,
  output [3:0] MenosSiginificativa
);

  RAM #(.addrWidth(7), .dataWidth(4)) ram_1 (.addr(in_1), .clk(in_3), .dout(MaisSignificativa));  // open: we, oe, din
  RAM #(.addrWidth(7), .dataWidth(4)) ram_2 (.addr(in_4), .clk(in_3), .dout(MenosSiginificativa));  // open: we, oe, din
  RAM ram_3 (.addr(in_2), .clk(in_3), .dout(out_6));  // open: we, oe, din
endmodule

module memRAMFFq4 (
  input  [2:0] in_1,
  output [3:0] out_2
);

  D_Flip_Flop d_ff_1 (.Q(out_2[3]));  // open: D, clk, Qn, preset, reset
  D_Flip_Flop d_ff_2 ();  // open: D, clk, Q, Qn, preset, reset
  D_Flip_Flop d_ff_3 ();  // open: D, clk, Q, Qn, preset, reset
  D_Flip_Flop d_ff_4 ();  // open: D, clk, Q, Qn, preset, reset
  D_Flip_Flop d_ff_5 ();  // open: D, clk, Q, Qn, preset, reset
  D_Flip_Flop d_ff_6 ();  // open: D, clk, Q, Qn, preset, reset
  D_Flip_Flop d_ff_7 ();  // open: D, clk, Q, Qn, preset, reset
  D_Flip_Flop d_ff_8 ();  // open: D, clk, Q, Qn, preset, reset
  D_Flip_Flop d_ff_9 (.Q(out_2[2]));  // open: D, clk, Qn, preset, reset
  D_Flip_Flop d_ff_10 ();  // open: D, clk, Q, Qn, preset, reset
  D_Flip_Flop d_ff_11 ();  // open: D, clk, Q, Qn, preset, reset
  D_Flip_Flop d_ff_12 ();  // open: D, clk, Q, Qn, preset, reset
  D_Flip_Flop d_ff_13 ();  // open: D, clk, Q, Qn, preset, reset
  D_Flip_Flop d_ff_14 ();  // open: D, clk, Q, Qn, preset, reset
  D_Flip_Flop d_ff_15 ();  // open: D, clk, Q, Qn, preset, reset
  D_Flip_Flop d_ff_16 ();  // open: D, clk, Q, Qn, preset, reset
  D_Flip_Flop d_ff_17 (.Q(out_2[1]));  // open: D, clk, Qn, preset, reset
  D_Flip_Flop d_ff_18 ();  // open: D, clk, Q, Qn, preset, reset
  D_Flip_Flop d_ff_19 ();  // open: D, clk, Q, Qn, preset, reset
  D_Flip_Flop d_ff_20 ();  // open: D, clk, Q, Qn, preset, reset
  D_Flip_Flop d_ff_21 ();  // open: D, clk, Q, Qn, preset, reset
  D_Flip_Flop d_ff_22 ();  // open: D, clk, Q, Qn, preset, reset
  D_Flip_Flop d_ff_23 ();  // open: D, clk, Q, Qn, preset, reset
  D_Flip_Flop d_ff_24 ();  // open: D, clk, Q, Qn, preset, reset
  D_Flip_Flop d_ff_25 (.Q(out_2[0]));  // open: D, clk, Qn, preset, reset
  D_Flip_Flop d_ff_26 ();  // open: D, clk, Q, Qn, preset, reset
  D_Flip_Flop d_ff_27 ();  // open: D, clk, Q, Qn, preset, reset
  D_Flip_Flop d_ff_28 ();  // open: D, clk, Q, Qn, preset, reset
  D_Flip_Flop d_ff_29 ();  // open: D, clk, Q, Qn, preset, reset
  D_Flip_Flop d_ff_30 ();  // open: D, clk, Q, Qn, preset, reset
  D_Flip_Flop d_ff_31 ();  // open: D, clk, Q, Qn, preset, reset
  D_Flip_Flop d_ff_32 ();  // open: D, clk, Q, Qn, preset, reset
  RAM ram_1 ();  // open: addr, we, oe, clk, din, dout
endmodule
